# Fritzing sketch schematic-vibrate-clock (saved by Fritzing 0.8.7b)
breadboards: 1

parts:
  Part2 = Arduino Fio (Funnel I/O)
  OLED1 = 128x32 I2C Monochrome OLED Display
  Part3 = Chronodot v2.1 DS3231
  U1 = Vibration Motor- ROB-08449 [package=vibe-motor-10mm]
  SP1 = SPEAKER [package=pcb_mount_speaker]
  S1 = Pushbutton [package="[THT]"]
  S2 = Pushbutton [package="[THT]"]
  R1 = Resistor [tolerance=±5% resistance=10k package="1206 [SMD]"]
  R2 = Resistor [tolerance=±5% resistance=10k package="1206 [SMD]"]
  R3 = Resistor [tolerance=±5% resistance=100 package=THT]
  MD03A1 = Dual VNH2SP30 Motor Driver [part_number=MD03A]
  S3 = Pushbutton [package="[THT]"]
  R4 = Resistor [tolerance=±5% resistance=10k package="1206 [SMD]"]
  S4 = Pushbutton [package="[THT]"]
  U2 = LIPO-1000mAh [package=lipo-1000]
  R5 = Resistor [tolerance=±5% resistance=1k package="1206 [SMD]"]  # not connected
  R6 = Resistor [tolerance=±5% resistance=1k package="1206 [SMD]"]

nets:
  VIN: Part2.VCC, OLED1.VIN, Part3.5V, S1.Pin_3, S1.Pin_4, S2.Pin_3, S2.Pin_4, MD03A1.VIN, S3.Pin_3, S3.Pin_4
  N1: Part2.D6_PWM, S3.Pin_1, S3.Pin_2, R4.Pin_0
  N2: Part2.D7, MD03A1.1CS
  N3: Part2.D9_PWM, R3.Pin_1
  GND: Part2.GND, OLED1.GND, Part3.GND, SP1.+, R1.Pin_1, R2.Pin_1, MD03A1.GND, R4.Pin_1
  N4: Part2.DTR_(Reset), S4.Pin_3, S4.Pin_4
  N5: Part2.A0, OLED1.RST
  N6: Part2.A1, R6.Pin_1
  N7: Part2.A2, MD03A1.1INa
  N8: Part2.A3, MD03A1.1INb
  N9: Part2.A4/SDA, S1.Pin_1, S1.Pin_2, R1.Pin_0
  N10: Part2.A5/SCL, S2.Pin_1, S2.Pin_2, R2.Pin_0
  N11: OLED1.SDA, Part3.SDA
  N12: OLED1.SCL, Part3.SCL
  N13: U1.+, MD03A1.OUT_1B
  N14: U1.-, MD03A1.OUT_1A
  N15: SP1.-, R3.Pin_0
  N16: S4.Pin_1, S4.Pin_2
  N17: U2.-, R6.Pin_0

custom parts:
  Chronodot v2.1 DS3231: Modified to DS3231 for naming purposes. This a custom designed module for the DS1307 Real Time Clock. The module comes fully assembled and pre-programmed with the current time (ok, so it's our current time - MST). The included Lithium coin cell battery (CR1225 41mAh) will run the module for a minimum of 9 years (17 years typical) without external 5V power. The DS1307 is accessed via the I2C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
